# Fritzing sketch Schema (saved by Fritzing 0.9.3b)
breadboards: 1

parts:
  Onderdeel2 = Arduino Mega 2560 (Rev3)
  M5 = Dagu DGServo 9g (Top view) [part_number="Lift tilt"]
  M4 = Dagu DGServo 9g (Top view) [part_number=Steering]
  M2 = DC Motor
  Use_small_version_of_the_L298N = H-Bridge with L298N
  M1 = DC Motor
  S2 = H-Bridge with L298N
  M3_Lift = DC Motor
  Regulator_5V = Voltage Regulator [part_number=7805 package=78xxl]
  Onderdeel3 = Bluetooth HC-05 Macho
  R3 = Resistor [tolerance=±5% resistance=1k package="0402 [SMD]"]
  R4 = Resistor [tolerance=±5% resistance=2.2k package="0402 [SMD]"]
  Part10 = ws2812b [package="smd 2812b"]
  7_4_Volt_LiPo = Power Jack [package=power_jack_slot]

nets:
  N1: Onderdeel2.D19/RX1, Onderdeel3.TXD
  N2: Onderdeel2.D18/TX1, R3.Pin_1
  GND: Onderdeel2.GND, M5.gnd, M4.gnd, S2.GND, Regulator_5V.GND, Onderdeel3.GND, R4.Pin_0, Part10.VSS, 7_4_Volt_LiPo.GND
  VIN: Onderdeel2.VIN, M5.vcc, S2.12V, Regulator_5V.IN, 7_4_Volt_LiPo.GNDBREAK
  N3: Onderdeel2.D2_PWM, Use_small_version_of_the_L298N.IN1
  N4: Onderdeel2.D3_PWM, Use_small_version_of_the_L298N.IN2
  N5: Onderdeel2.D4_PWM, Use_small_version_of_the_L298N.IN3
  N6: Onderdeel2.D5_PWM, Use_small_version_of_the_L298N.IN4
  N7: Onderdeel2.D6_PWM, S2.IN1
  N8: Onderdeel2.D7_PWM, S2.IN2
  N9: Onderdeel2.5V, M4.pulse
  N10: Onderdeel2.D22, M5.pulse
  N11: Onderdeel2.D26, Part10.DIN
  N12: M2.pin_1, Use_small_version_of_the_L298N.M1-02
  N13: M2.pin_2, Use_small_version_of_the_L298N.M1-01
  N14: Use_small_version_of_the_L298N.M2-01, M1.pin_2
  N15: Use_small_version_of_the_L298N.M2-02, M1.pin_1
  N16: S2.M1-01, M3_Lift.pin_2
  N17: S2.M1-02, M3_Lift.pin_1
  VCC: Regulator_5V.OUT, Onderdeel3.VCC, Part10.VDD
  N18: Onderdeel3.RXD, R3.Pin_0, R4.Pin_1

notes:
  WS2812B LED strip

custom parts:
  H-Bridge with L298N: h-bridge
